// Logisim project ALU.circ as structural Verilog: 2 circuits, main circuit ALU
module ALU (
  input  [31:0] A,
  input  [31:0] B,
  input  [4:0] Shift,
  input  [3:0] Codop,
  input  CarryIn,
  input  [30:0] in_6,
  input  [31:0] in_7,
  output [31:0] S,
  output [3:0] Flags
);

  wire adder_3_cout, bitselector_1_out, bitselector_2_out, bitselector_3_out, Bout, Cout, not_3_out, opShift;
  wire [3:0] subtractor_7_out;
  wire [4:0] subtractor_5_out, subtractor_6_out;
  wire [31:0] AandB, AandBBis, AfoisB, AorB, AplusB, AplusBplusCin, AplusBplusCinmoinsUn, AXorB, BandNotA,
       BmoinsA, BShiftArithmetic, BShiftLeft, BShiftRight, BShiftRotRight, not_1_out, notA, subtractor_1_out,
       ZeromoinsA;

  assign not_1_out = ~A;  // NOT_Gate not_1, 32 bits wide
  assign AandB = A & B;  // AND_Gate and_1, 32 bits wide
  assign AXorB = A ^ B;  // XOR_Gate xor_1, 32 bits wide
  Shifter #(.width(32)) shifter_1 (.in(B), .\dist (Shift), .out(BShiftLeft));
  Shifter #(.shift("lr"), .width(32)) shifter_2 (.in(B), .\dist (Shift), .out(BShiftRight));
  Shifter #(.shift("ar"), .width(32)) shifter_3 (.in(B), .\dist (Shift), .out(BShiftArithmetic));
  Adder #(.width(32)) adder_1 (.a(A), .b(B), .out(AplusBplusCin), .cin(CarryIn), .cout(Cout));
  Subtractor #(.width(32)) subtractor_1 (.a(A), .b(B), .out(subtractor_1_out), .bin(CarryIn), .bout(Bout));
  Shifter #(.shift("rr"), .width(32)) shifter_4 (.in(B), .\dist (Shift), .out(BShiftRotRight));
  assign AandBBis = A & B;  // AND_Gate and_2, 32 bits wide
  Subtractor #(.width(32)) subtractor_2 (.a({32{1'b0}}), .b(A), .out(ZeromoinsA));  // open: bin, bout
  Subtractor #(.width(32)) subtractor_3 (.a(B), .b(A), .out(BmoinsA));  // open: bin, bout
  Adder #(.width(32)) adder_2 (.a(A), .b(B), .out(AplusB));  // open: cin, cout
  assign AorB = A | B;  // OR_Gate or_1, 32 bits wide
  Multiplier #(.width(32)) multiplier_1 (.a(A), .b(B), .out(AfoisB));  // open: cin, cout
  assign BandNotA = not_1_out & B;  // AND_Gate and_3, 32 bits wide
  assign notA = ~A;  // NOT_Gate not_2, 32 bits wide
  Subtractor #(.width(32)) subtractor_4 (
    .a(subtractor_1_out), .b(32'h1), .out(AplusBplusCinmoinsUn));  // open: bin, bout
  Multiplexer #(.enable("true"), .select(4), .width(32)) multiplexer_1 (
    .in0(AandB), .in1(AXorB), .in2(BShiftLeft), .in3(BShiftRight), .in4(BShiftArithmetic),
    .in5(AplusBplusCin), .in6(AplusBplusCinmoinsUn), .in7(BShiftRotRight), .in8(AandBBis), .in9(ZeromoinsA),
    .in10(BmoinsA), .in11(AplusB), .in12(AorB), .in13(AfoisB), .in14(BandNotA), .in15(notA),
    .out({Flags[3], S[30:0]}), .sel(Codop));  // open: en
  Adder #(.width(32)) adder_3 (.a(notA), .b(in_7), .cout(adder_3_cout));  // open: out, cin
  Subtractor #(.width(5)) subtractor_5 (.a({5{1'b0}}), .b(Shift), .out(subtractor_5_out));  // open: bin, bout
  Subtractor #(.width(5)) subtractor_6 (.a(Shift), .b(5'b00001), .out(subtractor_6_out));  // open: bin, bout
  not not_3 (not_3_out, Bout);
  BitSelector #(.width(32)) bitselector_1 (.in(B), .out(bitselector_1_out), .sel(subtractor_6_out));
  BitSelector #(.width(32)) bitselector_2 (.in(B), .out(bitselector_2_out), .sel(subtractor_5_out));
  Multiplexer #(.enable("true"), .select(4)) multiplexer_2 (
    .in2(opShift), .in3(opShift), .in5(Cout), .in6(not_3_out), .in9(adder_3_cout), .in10(not_3_out),
    .in11(Cout), .out(Flags[1]), .sel(Codop));  // open: in0, in1, in4, in7, in8, in12, in13, in14, in15, en
  Multiplexer multiplexer_3 (.in0(bitselector_1_out), .in1(bitselector_2_out), .out(opShift), .sel(bitselector_3_out));
  Subtractor #(.width(4)) subtractor_7 (.a(Codop), .b(4'b0010), .out(subtractor_7_out));  // open: bin, bout
  Comparator #(.width(31)) comparator_1 (.a(in_6), .b(S[30:0]), .eq(Flags[0]));  // open: gt, lt
  BitSelector #(.width(4)) bitselector_3 (.in(subtractor_7_out), .out(bitselector_3_out), .sel(2'b00));

  assign S[31] = Flags[3];

  // Other names for the same wires on the sheet: Cin = CarryIn; Z = Flags[0]; C = Flags[1];
  //   Sortie[31:0] = {Flags[3], S[30:0]}

  // Notes on the sheet:
  //   A: initial=0x560
  //   B: initial=0x5645
  //   in_7: initial=0x1
  //   Note: for ROR, C = N
  //   Note 2: assume that shift > 0 for LSL and LSR
endmodule

module test (
  input  [4:0] Shift,
  input  [3:0] Codop,
  input  [3:0] in_3,
  input  CarryIn,
  output [31:0] out_5
);

  ALU alu_1 (
    .A(32'h8), .B(32'h8), .Shift(Shift), .Codop(Codop), .CarryIn(CarryIn), .S(out_5), .Flags(in_3));  // open: in_6, in_7
endmodule
